# Fritzing sketch UNO_SRF05_LCDI2C (saved by Fritzing 0.8.5b)
breadboards: 1

parts:
  Εξάρτημα1 = Arduino Uno (Rev3)
  LCM1602_IIC1 = LCM1602 IIC [part_number="LCM1602 IIC" chip_label="LCM1602 IIC" package="DIP (Dual Inline) [THT]"]
  LCD1 = LCD screen
  Parte4 = SRF05 Ultrasonic Rangefinder
  S1 = Pushbutton [package="[THT]"]

nets:
  N1: Εξάρτημα1.A4/SDA, LCM1602_IIC1.SDA
  N2: Εξάρτημα1.A5/SCL, LCM1602_IIC1.SCL
  N3: Εξάρτημα1.D8, Parte4.Trig
  GND: Εξάρτημα1.GND, LCM1602_IIC1.GND, Parte4.GND, S1.Pin_1, S1.Pin_2
  N4: Εξάρτημα1.D2, S1.Pin_3, S1.Pin_4
  N5: Εξάρτημα1.D7, Parte4.Echo
  VCC: Εξάρτημα1.5V, LCM1602_IIC1.VCC, Parte4.VCC
  VSS: LCM1602_IIC1.VSS, LCD1.VSS
  VDD: LCM1602_IIC1.VDD, LCD1.VDD
  N6: LCM1602_IIC1.V0, LCD1.V0
  N7: LCM1602_IIC1.RS, LCD1.RS
  N8: LCM1602_IIC1.RW, LCD1.R/W
  N9: LCM1602_IIC1.E, LCD1.E
  N10: LCM1602_IIC1.D0, LCD1.DB0
  N11: LCM1602_IIC1.D1, LCD1.DB1
  N12: LCM1602_IIC1.D2, LCD1.DB2
  N13: LCM1602_IIC1.D3, LCD1.DB3
  N14: LCM1602_IIC1.D4, LCD1.DB4
  N15: LCM1602_IIC1.D5, LCD1.DB5
  N16: LCM1602_IIC1.D6, LCD1.DB6
  N17: LCM1602_IIC1.D7, LCD1.DB7
  N18: LCM1602_IIC1.A, LCD1.LED+
  N19: LCM1602_IIC1.K, LCD1.LED-

notes:
  Module RS232 to TTL
  (Max3232; 3-5VDC)
  VCC RXD TXD GND
  Port COM PC

custom parts:
  LCM1602 IIC: I2C-Module to use a 1602 or 2004 LCD on with the wire.h libory Serial LCD Modul
